# Fritzing sketch layout (saved by Fritzing 0.9.3b)

parts:
  Sensor_PIR_HC-SR501 = HC-SR501 Body Sensor Module
  Raspberry_Pi_Zero1 = Raspberry Pi Zero

nets:
  VCC: Sensor_PIR_HC-SR501.VCC, Raspberry_Pi_Zero1.5V
  N1: Sensor_PIR_HC-SR501.OUT, Raspberry_Pi_Zero1.GPIO14
  GND: Sensor_PIR_HC-SR501.GND, Raspberry_Pi_Zero1.GND

notes:
  +5V
  GND
  GPIO14
  RASPBERRY PI ZERO W

custom parts:
  HC-SR501 Body Sensor Module: Pyroelectric Infrared PIR Motion Sensor Detector Module
